# Fritzing sketch diagram (saved by Fritzing 0.9.3b)
breadboards: 1

parts:
  Part1 = Arduino Nano (Rev3.0)
  S1 = H-Bridge with L298N
  VCC1 = Battery
  VCC2 = Battery
  VCC3 = Battery
  VCC4 = Battery
  M1 = DC Motor
  M2 = DC Motor
  hc-sr1 = hc-sr04

nets:
  GND: Part1.GND, S1.GND, VCC4.-, hc-sr1.GND
  N1: Part1.D3, hc-sr1.Trig
  N2: Part1.D4, hc-sr1.Echo
  N3: Part1.D5, S1.ENB
  N4: Part1.D6, S1.IN4
  N5: Part1.D7, S1.IN3
  N6: Part1.D8, S1.IN2
  N7: Part1.D9, S1.IN1
  N8: Part1.D10, S1.ENA
  5V: Part1.5V, S1.5V, hc-sr1.VCC
  N9: S1.12V, VCC1.+
  N10: S1.M1-01, M2.pin_2
  N11: S1.M1-02, M2.pin_1
  N12: S1.M2-01, M1.pin_2
  N13: S1.M2-02, M1.pin_1
  N14: VCC1.-, VCC2.+
  N15: VCC2.-, VCC3.+
  N16: VCC3.-, VCC4.+

custom parts:
  H-Bridge with L298N: h-bridge
